// Logisim project cpu-rebuild.circ as structural Verilog: 8 circuits, main circuit main
module main (
  input  RESET
);

  wire and_1_out, and_2_out, and_3_out, and_4_out, and_5_out, and_6_out, and_7_out, and_8_out, and_9_out,
       and_10_out, and_11_out, and_13_out, and_14_out, clock_1_out, decoder_1_out0, decoder_1_out1,
       decoder_1_out2, decoder_1_out9, decoder_1_out10, decoder_1_out11, decoder_1_out14, decoder_1_out15,
       decoder_2_out0, decoder_2_out1, decoder_2_out2, decoder_2_out9, decoder_2_out10, decoder_2_out14,
       decoder_2_out15, decoder_3_out0, decoder_3_out1, decoder_3_out2, decoder_3_out9, decoder_3_out10,
       decoder_3_out14, decoder_3_out15, instrdecoder_1_add, instrdecoder_1_bitnand, instrdecoder_1_carryen,
       instrdecoder_1_cmp, instrdecoder_1_immir1, instrdecoder_1_immir2, instrdecoder_1_jmp,
       instrdecoder_1_jmpcarry, instrdecoder_1_jmpneg, instrdecoder_1_jmpover, instrdecoder_1_jmpzero,
       instrdecoder_1_load, instrdecoder_1_loadrel, instrdecoder_1_pop, instrdecoder_1_programload,
       instrdecoder_1_push, instrdecoder_1_ret, instrdecoder_1_stop, instrdecoder_1_store,
       instrdecoder_1_storerel, instrdecoder_1_sub, instrfetchring_1_finished, instrfetchring_1_writeir0,
       instrfetchring_1_writeir1, instrfetchring_1_writeir2, instrlendec_1_len1, instrlendec_1_len2,
       instrlendec_1_len3, instrstagering_1_decsp, instrstagering_1_finished, instrstagering_1_genericstage,
       instrstagering_1_incsp, instrstagering_1_setbptosp, instrstagering_1_setsptobpdec,
       instrstagering_1_stackloadbp, instrstagering_1_stackloadreg, instrstagering_1_stackstorebp,
       instrstagering_1_stackstorereg, MemRead_out, MemRelAddr_out, MemWrite_out, nand_1_out, nand_2_out,
       nand_3_out, nand_4_out, nand_5_out, nand_6_out, nor_1_out, nor_2_out, nor_3_out, nor_4_out, nor_5_out,
       not_1_out, not_2_out, not_3_out, not_4_out, not_5_out, not_6_out, not_7_out, not_8_out, not_9_out,
       not_10_out, not_11_out, not_12_out, or_1_out, or_2_out, or_3_out, or_4_out, or_5_out, or_6_out,
       or_7_out, or_8_out, or_9_out, or_10_out, or_11_out, or_12_out, or_13_out, or_14_out, or_15_out,
       RegWE_out, RegWEStep_out, rgb_video_1_p1, rgb_video_1_p2, StackOp_out;
  wire [1:0] instrdecoder_1_call, instrstagering_1_setpc, instrstagering_1_stackloadpc,
       instrstagering_1_stackstorepc;
  wire [3:0] alu_1_zero, FLAGS_q, IR0_q, IR0_q_2, IR1_q, IR1_q_2, pc_1_q, pc_1_q_2, pc_1_q_3, pc_1_q_4;
  wire [5:0] rgb_video_1_p4, rgb_video_1_p5;
  wire [7:0] alu_1_result, BP_q, controlled_buffer_1_out, controlled_buffer_4_out, controlled_buffer_9_out,
       IR2_q, multiplexer_1_out, multiplexer_2_out, multiplexer_5_out, multiplexer_6_out, multiplexer_7_out,
       multiplexer_8_out, multiplexer_10_out, multiplexer_11_out, ram_1_dout, RegA_q, RegB_q, RegC_q,
       rom_1_data, SP_q;
  wire [15:0] ADDR_q, multiplexer_4_out, multiplexer_9_out, pull_resistor_1_node;

  Clock clock_1 (.out(clock_1_out));
  and and_1 (and_1_out, nand_1_out, clock_1_out);
  Multiplexer #(.width(8)) multiplexer_1 (
    .in0(IR2_q), .in1(ram_1_dout), .out(multiplexer_1_out), .sel(instrstagering_1_stackloadpc[0]));
  or or_1 (or_1_out, and_8_out, RESET, and_2_out, and_10_out);
  or or_2 (or_2_out, RESET, and_7_out, and_2_out, and_10_out);
  assign controlled_buffer_1_out = instrstagering_1_stackstorepc[1] ? {pc_1_q_4, pc_1_q_3} : 8'bz;  // Controlled_Buffer controlled_buffer_1
  or or_3 (or_3_out, and_3_out, RegWEStep_out);
  Decoder #(.select(4)) decoder_1 (
    .out0(decoder_1_out0), .out1(decoder_1_out1), .out2(decoder_1_out2), .out9(decoder_1_out9),
    .out10(decoder_1_out10), .out11(decoder_1_out11), .out14(decoder_1_out14), .out15(decoder_1_out15),
    .sel(IR0_q), .en(or_3_out));  // open: out3, out4, out5, out6, out7, out8, out12, out13
  not not_1 (not_1_out, RESET);
  Multiplexer #(.width(8)) multiplexer_2 (
    .in0({IR1_q_2, IR1_q}), .in1(ram_1_dout), .out(multiplexer_2_out), .sel(instrstagering_1_stackloadpc[1]));
  Pull_Resistor pull_resistor_1 (.node(pull_resistor_1_node));
  assign pull_resistor_1_node = not_1_out ? multiplexer_4_out : 16'bz;  // Controlled_Buffer controlled_buffer_2
  and and_2 (and_2_out, and_1_out, or_5_out);
  nor nor_1 (nor_1_out, nor_2_out, instrdecoder_1_immir1);
  or or_4 (or_4_out, instrstagering_1_setsptobpdec, or_6_out);
  assign controlled_buffer_1_out = instrstagering_1_stackstorepc[0] ? {pc_1_q_2, pc_1_q} : 8'bz;  // Controlled_Buffer controlled_buffer_3
  assign controlled_buffer_4_out = or_4_out ? 8'h1 : 8'bz;  // Controlled_Buffer controlled_buffer_4
  Pull_Resistor pull_resistor_2 (.node(controlled_buffer_1_out));
  Pull_Resistor pull_resistor_3 (.node(controlled_buffer_4_out));
  Multiplexer #(.width(8)) multiplexer_3 (
    .in0(multiplexer_2_out), .in1(ADDR_q[15:8]), .out(multiplexer_4_out[15:8]),
    .sel(instrstagering_1_setpc[1]));
  Multiplexer #(.width(8)) multiplexer_4 (
    .in0(multiplexer_1_out), .in1(ADDR_q[7:0]), .out(multiplexer_4_out[7:0]), .sel(instrstagering_1_setpc[1]));
  or or_5 (or_5_out, instrstagering_1_setpc[0], instrstagering_1_setpc[1]);
  nand nand_1 (nand_1_out, instrfetchring_1_finished, instrdecoder_1_stop);
  InstrDecoder instrdecoder_1 (
    .Instr({IR0_q_2, IR0_q}), .Stop(instrdecoder_1_stop), .Add(instrdecoder_1_add), .Sub(instrdecoder_1_sub),
    .CarryEn(instrdecoder_1_carryen), .BitNAND(instrdecoder_1_bitnand), .Cmp(instrdecoder_1_cmp),
    .ImmIR1(instrdecoder_1_immir1), .ImmIR2(instrdecoder_1_immir2), .Jmp(instrdecoder_1_jmp),
    .JmpZero(instrdecoder_1_jmpzero), .JmpNeg(instrdecoder_1_jmpneg), .JmpCarry(instrdecoder_1_jmpcarry),
    .JmpOver(instrdecoder_1_jmpover), .Push(instrdecoder_1_push), .Pop(instrdecoder_1_pop),
    .Ret(instrdecoder_1_ret), .Call(instrdecoder_1_call), .StoreRel(instrdecoder_1_storerel),
    .LoadRel(instrdecoder_1_loadrel), .Store(instrdecoder_1_store), .Load(instrdecoder_1_load),
    .ProgramLoad(instrdecoder_1_programload));
  Decoder #(.select(4)) decoder_2 (
    .out0(decoder_2_out0), .out1(decoder_2_out1), .out2(decoder_2_out2), .out9(decoder_2_out9),
    .out10(decoder_2_out10), .out14(decoder_2_out14), .out15(decoder_2_out15), .sel(IR1_q_2), .en(nor_1_out));  // open: out3, out4, out5, out6, out7, out8, out11, out12, out13
  assign controlled_buffer_4_out = instrdecoder_1_immir2 ? IR2_q : 8'bz;  // Controlled_Buffer controlled_buffer_5
  assign controlled_buffer_1_out = instrdecoder_1_immir1 ? {IR1_q_2, IR1_q} : 8'bz;  // Controlled_Buffer controlled_buffer_6
  PC pc_1 (
    .Addr(pull_resistor_1_node), .OverwriteHIGH(or_1_out), .OverwriteLOW(or_2_out), .CLK(nor_4_out),
    .Q({pc_1_q_4, pc_1_q_3, pc_1_q_2, pc_1_q}));
  and and_3 (and_3_out, instrstagering_1_genericstage, RegWE_out);
  or RegWE (RegWE_out, instrdecoder_1_programload, instrdecoder_1_load, instrdecoder_1_loadrel, instrdecoder_1_immir1, instrdecoder_1_add, instrdecoder_1_sub, instrdecoder_1_bitnand);
  or or_6 (or_6_out, instrstagering_1_incsp, instrstagering_1_decsp);
  nor nor_2 (nor_2_out, instrstagering_1_genericstage, instrstagering_1_stackstorereg);
  Register RegA (.D(multiplexer_5_out), .en(decoder_1_out0), .clk(and_1_out), .Q(RegA_q), .clr(RESET));
  Hex_Digit_Display hex_digit_display_1 (.value(pc_1_q_4));  // open: dp
  not not_2 (not_2_out, not_3_out);
  not not_3 (not_3_out, not_4_out);
  not not_4 (not_4_out, instrfetchring_1_finished);
  and and_4 (and_4_out, not_2_out, instrfetchring_1_finished, and_6_out);
  not not_5 (not_5_out, instrdecoder_1_immir2);
  and and_5 (and_5_out, not_5_out, instrstagering_1_genericstage);
  assign controlled_buffer_1_out = decoder_2_out0 ? RegA_q : 8'bz;  // Controlled_Buffer controlled_buffer_7
  assign controlled_buffer_4_out = decoder_3_out0 ? RegA_q : 8'bz;  // Controlled_Buffer controlled_buffer_8
  assign controlled_buffer_9_out = decoder_1_out9 ? multiplexer_5_out : 8'bz;  // Controlled_Buffer controlled_buffer_9
  Hex_Digit_Display hex_digit_display_2 (.value(pc_1_q_3));  // open: dp
  InstrLenDec instrlendec_1 (
    .Instr({IR0_q_2, IR0_q}), .Len3(instrlendec_1_len3), .Len2(instrlendec_1_len2), .Len1(instrlendec_1_len1));
  or or_7 (or_7_out, RESET, and_9_out);
  and and_6 (and_6_out, and_1_out, instrfetchring_1_finished);
  not not_6 (not_6_out, or_7_out);
  Decoder #(.select(4)) decoder_3 (
    .out0(decoder_3_out0), .out1(decoder_3_out1), .out2(decoder_3_out2), .out9(decoder_3_out9),
    .out10(decoder_3_out10), .out14(decoder_3_out14), .out15(decoder_3_out15), .sel(IR1_q), .en(and_5_out));  // open: out3, out4, out5, out6, out7, out8, out11, out12, out13
  Register RegB (.D(multiplexer_5_out), .en(decoder_1_out1), .clk(and_1_out), .Q(RegB_q), .clr(RESET));
  Hex_Digit_Display hex_digit_display_3 (.value(pc_1_q_2));  // open: dp
  Hex_Digit_Display hex_digit_display_4 (.value(pc_1_q));  // open: dp
  not not_7 (not_7_out, not_6_out);
  not not_8 (not_8_out, not_7_out);
  nor nor_3 (nor_3_out, not_8_out, or_7_out);
  or or_8 (or_8_out, nor_3_out, and_4_out);
  assign controlled_buffer_1_out = decoder_2_out1 ? RegB_q : 8'bz;  // Controlled_Buffer controlled_buffer_10
  assign controlled_buffer_4_out = decoder_3_out1 ? RegB_q : 8'bz;  // Controlled_Buffer controlled_buffer_11
  and and_7 (and_7_out, instrstagering_1_stackloadpc[0], and_1_out);
  Register RegC (.D(multiplexer_5_out), .en(decoder_1_out2), .clk(and_1_out), .Q(RegC_q), .clr(RESET));
  and and_8 (and_8_out, instrstagering_1_stackloadpc[1], and_1_out);
  assign controlled_buffer_1_out = decoder_2_out2 ? RegC_q : 8'bz;  // Controlled_Buffer controlled_buffer_12
  assign controlled_buffer_4_out = decoder_3_out2 ? RegC_q : 8'bz;  // Controlled_Buffer controlled_buffer_13
  InstrFetchRing instrfetchring_1 (
    .InstrLen3(instrlendec_1_len3), .InstrLen2(instrlendec_1_len2), .InstrLen1(instrlendec_1_len1),
    .RST(or_7_out), .CLK(and_1_out), .WriteIR0(instrfetchring_1_writeir0),
    .WriteIR1(instrfetchring_1_writeir1), .WriteIR2(instrfetchring_1_writeir2),
    .Finished(instrfetchring_1_finished));
  not not_9 (not_9_out, and_1_out);
  InstrStageRing instrstagering_1 (
    .Call(instrdecoder_1_call), .Ret(instrdecoder_1_ret), .Pop(instrdecoder_1_pop),
    .Push(instrdecoder_1_push), .RST(or_8_out), .CLK(and_6_out),
    .GenericStage(instrstagering_1_genericstage), .StackStorePC(instrstagering_1_stackstorepc),
    .SetSPtoBPDec(instrstagering_1_setsptobpdec), .StackLoadPC(instrstagering_1_stackloadpc),
    .SetBPtoSP(instrstagering_1_setbptosp), .SetPC(instrstagering_1_setpc), .IncSP(instrstagering_1_incsp),
    .DecSP(instrstagering_1_decsp), .StackStoreBP(instrstagering_1_stackstorebp),
    .StackLoadBP(instrstagering_1_stackloadbp), .StackStoreReg(instrstagering_1_stackstorereg),
    .StackLoadReg(instrstagering_1_stackloadreg), .Finished(instrstagering_1_finished));
  or or_9 (or_9_out, decoder_1_out10, instrstagering_1_decsp, instrstagering_1_incsp, instrstagering_1_setsptobpdec);
  Register SP (.D(multiplexer_5_out), .en(or_9_out), .clk(and_1_out), .Q(SP_q), .clr(RESET));
  nor nor_4 (nor_4_out, instrfetchring_1_finished, not_9_out);
  and and_9 (and_9_out, instrfetchring_1_finished, instrstagering_1_finished);
  or or_10 (or_10_out, instrstagering_1_decsp, decoder_2_out9, instrstagering_1_setbptosp, instrstagering_1_incsp);
  or StackOp (StackOp_out, instrstagering_1_stackstorebp, instrstagering_1_stackloadbp, instrstagering_1_stackstorereg, instrstagering_1_stackloadreg, instrstagering_1_stackstorepc[1], instrstagering_1_stackstorepc[0], instrstagering_1_stackloadpc[0], instrstagering_1_stackloadpc[1]);
  or or_11 (or_11_out, decoder_1_out11, instrstagering_1_setbptosp, instrstagering_1_stackloadbp);
  assign controlled_buffer_1_out = or_10_out ? SP_q : 8'bz;  // Controlled_Buffer controlled_buffer_14
  assign controlled_buffer_4_out = decoder_3_out9 ? SP_q : 8'bz;  // Controlled_Buffer controlled_buffer_15
  or RegWEStep (RegWEStep_out, instrstagering_1_setbptosp, instrstagering_1_stackloadreg, instrstagering_1_stackloadbp, instrstagering_1_setsptobpdec);
  Register BP (.D(multiplexer_5_out), .en(or_11_out), .clk(and_1_out), .Q(BP_q), .clr(RESET));
  or MemWrite (MemWrite_out, instrstagering_1_stackstorepc[1], instrstagering_1_stackstorepc[0], instrstagering_1_stackstorebp, instrstagering_1_stackstorereg, instrdecoder_1_storerel, instrdecoder_1_store);
  or or_12 (or_12_out, decoder_2_out10, instrstagering_1_setsptobpdec, instrstagering_1_stackstorebp);
  assign controlled_buffer_1_out = or_12_out ? BP_q : 8'bz;  // Controlled_Buffer controlled_buffer_16
  assign controlled_buffer_4_out = decoder_3_out10 ? BP_q : 8'bz;  // Controlled_Buffer controlled_buffer_17
  Register IR0 (.D(rom_1_data), .en(instrfetchring_1_writeir0), .clk(nor_4_out), .Q({IR0_q_2, IR0_q}), .clr(or_7_out));
  Register BANK (.D(multiplexer_5_out), .en(decoder_1_out14), .clk(and_1_out), .Q(ADDR_q[15:8]), .clr(RESET));
  or MemRead (MemRead_out, instrstagering_1_stackloadpc[0], instrstagering_1_stackloadpc[1], instrstagering_1_stackloadbp, instrstagering_1_stackloadreg, instrdecoder_1_loadrel, instrdecoder_1_load);
  assign controlled_buffer_1_out = decoder_2_out14 ? ADDR_q[15:8] : 8'bz;  // Controlled_Buffer controlled_buffer_18
  assign controlled_buffer_4_out = decoder_3_out14 ? ADDR_q[15:8] : 8'bz;  // Controlled_Buffer controlled_buffer_19
  Register IR1 (.D(rom_1_data), .en(instrfetchring_1_writeir1), .clk(nor_4_out), .Q({IR1_q_2, IR1_q}), .clr(or_7_out));
  or MemRelAddr (MemRelAddr_out, instrdecoder_1_loadrel, instrdecoder_1_storerel);
  or or_13 (or_13_out, instrstagering_1_stackstorepc[0], instrstagering_1_stackstorepc[1], instrstagering_1_stackstorereg, instrstagering_1_setbptosp, instrstagering_1_stackstorebp, instrdecoder_1_immir1, instrdecoder_1_store);
  Register ADDR (.D(multiplexer_5_out), .en(decoder_1_out15), .clk(and_1_out), .Q(ADDR_q[7:0]), .clr(RESET));
  Multiplexer #(.width(8)) multiplexer_5 (
    .in0(multiplexer_6_out), .in1(rom_1_data), .out(multiplexer_5_out), .sel(instrdecoder_1_programload));
  assign controlled_buffer_1_out = decoder_2_out15 ? ADDR_q[7:0] : 8'bz;  // Controlled_Buffer controlled_buffer_20
  assign controlled_buffer_4_out = decoder_3_out15 ? ADDR_q[7:0] : 8'bz;  // Controlled_Buffer controlled_buffer_21
  Multiplexer #(.width(8)) multiplexer_6 (
    .in0(alu_1_result), .in1(ram_1_dout), .out(multiplexer_6_out), .sel(MemRead_out));
  Register IR2 (.D(rom_1_data), .en(instrfetchring_1_writeir2), .clk(nor_4_out), .Q(IR2_q), .clr(or_7_out));
  nand nand_2 (nand_2_out, not_10_out, nand_3_out, nand_4_out, nand_5_out, nand_6_out);
  nand nand_3 (nand_3_out, instrdecoder_1_jmpzero, FLAGS_q[0]);
  not not_10 (not_10_out, instrdecoder_1_jmp);
  or or_14 (or_14_out, instrdecoder_1_cmp, instrstagering_1_decsp, instrstagering_1_setsptobpdec, instrdecoder_1_sub);
  Multiplexer #(.width(8)) multiplexer_7 (
    .in0(ADDR_q[15:8]), .in1({8{1'b1}}), .out(multiplexer_7_out), .sel(StackOp_out));
  Multiplexer #(.width(8)) multiplexer_8 (.in0(ADDR_q[7:0]), .in1(SP_q), .out(multiplexer_8_out), .sel(StackOp_out));
  and and_10 (and_10_out, nand_2_out, instrstagering_1_genericstage);
  nand nand_4 (nand_4_out, instrdecoder_1_jmpcarry, FLAGS_q[1]);
  nand nand_5 (nand_5_out, instrdecoder_1_jmpover, FLAGS_q[2]);
  or or_15 (or_15_out, instrdecoder_1_cmp, instrdecoder_1_sub, instrdecoder_1_add);
  Register #(.width(4)) FLAGS (.D(alu_1_zero), .en(and_11_out), .clk(and_1_out), .Q(FLAGS_q), .clr(RESET));
  and and_11 (and_11_out, instrstagering_1_genericstage, or_15_out);
  Multiplexer #(.width(16)) multiplexer_9 (
    .in0({pc_1_q_4, pc_1_q_3, pc_1_q_2, pc_1_q}), .in1(ADDR_q), .out(multiplexer_9_out),
    .sel(instrdecoder_1_programload));
  Multiplexer #(.width(8)) multiplexer_10 (
    .in0(multiplexer_8_out), .in1(alu_1_result), .out(multiplexer_10_out), .sel(MemRelAddr_out));
  nand nand_6 (nand_6_out, instrdecoder_1_jmpneg, FLAGS_q[3]);
  Multiplexer #(.width(8)) multiplexer_11 (
    .in0(alu_1_result), .in1(RegA_q), .out(multiplexer_11_out), .sel(instrdecoder_1_storerel));
  ALU alu_1 (
    .Passthrough(or_13_out), .CarryFlag(FLAGS_q[1]), .CarryEn(instrdecoder_1_carryen),
    .A(controlled_buffer_1_out), .B(controlled_buffer_4_out), .Subtract(or_14_out),
    .BitNAND(instrdecoder_1_bitnand), .Result(alu_1_result), .Zero(alu_1_zero[0]), .CarryOut(alu_1_zero[1]),
    .Overflow(alu_1_zero[2]), .Negative(alu_1_zero[3]));
  RAM #(.addrWidth(16), .asyncread("true"), .clearpin("true")) ram_1 (
    .addr({multiplexer_7_out, multiplexer_10_out}), .we(MemWrite_out), .oe(MemRead_out), .clk(and_1_out),
    .din(multiplexer_11_out), .dout(ram_1_dout), .clr(RESET));
  ROM #(.addrWidth(16)) rom_1 (.addr(multiplexer_9_out), .data(rom_1_data));
  Pull_Resistor pull_resistor_4 (.node(controlled_buffer_9_out));
  // RGB_Video #(.cursor("No Cursor"), .height(64), .scale(8), .width(64)) rgb_video_1: pin names not known; wires that end beside it: rgb_video_1_p1, rgb_video_1_p2, rgb_video_1_p2, rgb_video_1_p4, rgb_video_1_p5, controlled_buffer_9_out[3:0]
  nor nor_5 (nor_5_out, controlled_buffer_9_out[6], controlled_buffer_9_out[7]);
  nor nor_6 (rgb_video_1_p2, and_14_out, and_13_out, nor_5_out);
  and and_12 (rgb_video_1_p1, nor_5_out, controlled_buffer_9_out[0]);
  Register #(.width(6)) register_1 (
    .D(controlled_buffer_9_out[5:0]), .en(and_13_out), .clk(and_13_out), .Q(rgb_video_1_p4));  // open: clr
  and and_13 (and_13_out, controlled_buffer_9_out[6], not_11_out);
  not not_11 (not_11_out, controlled_buffer_9_out[7]);
  not not_12 (not_12_out, controlled_buffer_9_out[6]);
  Register #(.width(6)) register_2 (
    .D(controlled_buffer_9_out[5:0]), .en(and_14_out), .clk(and_14_out), .Q(rgb_video_1_p5));  // open: clr
  and and_14 (and_14_out, not_12_out, controlled_buffer_9_out[7]);

  // Notes on the sheet:
  //   contents of rom_1 (hex, n*v repeats v):
  //   e0 0 ca 10 20 a2 0 42 20 d1 10 1 10 20 a2 0 12 12 22 e1 0 19 e0 0 7 c0 20 0 22 1 10 20 a2 0 40 0 d1
  //   10 1 12 12 e1 0 2f e0 0 22 22 1 10 20 a2 0 40 0 e4 0 3d e0 0 40 c0 0 1 d1 10 1 12 12 e1 0 4b e0 0 35
  //   22 1 10 20 a2 8 72 21 c1 20 0 ea 0 31 22 1 10 f0 10 20 a2 0 11 0 cf f0 1 d1 10 1 12 12 e1 0 71 e0 0
  //   61 22 2f 1 10 f0 10 20 a2 0 10 0 90 f2 60 12 20 c2 20 1 12 2 e1 0 8c e0 0 7a 22 2f 1 10 e0 10 f0 10
  //   20 ae ff a2 0 10 20 10 0 90 f2 92 12 12 2 e1 0 ab a0 0 e0 0 c4 a0 2 90 b0 c0 0 1 a2 3 92 b2 12 20 e1
  //   0 c2 a2 2 60 b2 e0 0 9d a0 1 22 22 22 2f 2e 1 a0 0 a1 0 c0 0 1 c1 10 1 a9 1 a2 40 10 0 b2 22 b0 0 b2
  //   2 20 c9 20 0 a2 80 10 10 b2 22 b1 11 b2 12 21 c9 20 0 a9 cf e0 0 ce
endmodule

module ALU (
  input  Passthrough,
  input  CarryFlag,
  input  CarryEn,
  input  [7:0] A,
  input  [7:0] B,
  input  Subtract,
  input  BitNAND,
  output [7:0] Result,
  output Zero,
  output CarryOut,
  output Overflow,
  output Negative
);

  wire and_1_out, nor_1_out, nor_6_out, nor_11_out, nor_12_out, nor_13_out, nor_14_out, nor_15_out,
       nor_16_out, nor_17_out, not_1_out, not_2_out, not_3_out, not_4_out, not_5_out, not_6_out, not_7_out,
       not_8_out, not_9_out, not_10_out, xor_1_out, xor_2_out, xor_3_out, xor_4_out, xor_5_out, xor_6_out,
       xor_7_out, xor_8_out;
  wire [6:0] adder_1_out;
  wire [7:0] nand_1_out, nor_2_out;

  not not_1 (not_1_out, BitNAND);
  nor nor_1 (nor_1_out, not_1_out, Passthrough);
  xor xor_1 (xor_1_out, B[0], Subtract);
  xor xor_2 (xor_2_out, B[1], Subtract);
  xor xor_3 (xor_3_out, B[2], Subtract);
  xor xor_4 (xor_4_out, B[3], Subtract);
  not not_2 (not_2_out, xor_1_out);
  not not_3 (not_3_out, xor_2_out);
  not not_4 (not_4_out, xor_3_out);
  not not_5 (not_5_out, xor_4_out);
  nor nor_2 (nor_2_out[0], not_2_out, Passthrough);
  nor nor_3 (nor_2_out[1], not_3_out, Passthrough);
  nor nor_4 (nor_2_out[2], not_4_out, Passthrough);
  nor nor_5 (nor_2_out[3], not_5_out, Passthrough);
  nand nand_1 (nand_1_out[0], A[0], B[0]);
  nand nand_2 (nand_1_out[1], A[1], B[1]);
  nand nand_3 (nand_1_out[2], A[2], B[2]);
  nand nand_4 (nand_1_out[3], A[3], B[3]);
  not not_6 (not_6_out, Subtract);
  xor xor_5 (xor_5_out, B[4], Subtract);
  not not_7 (not_7_out, xor_5_out);
  xor xor_6 (xor_6_out, B[5], Subtract);
  not not_8 (not_8_out, xor_6_out);
  xor xor_7 (xor_7_out, B[6], Subtract);
  not not_9 (not_9_out, xor_7_out);
  xor xor_8 (xor_8_out, B[7], Subtract);
  not not_10 (not_10_out, xor_8_out);
  nand nand_5 (nand_1_out[4], A[4], B[4]);
  nand nand_6 (nand_1_out[5], A[5], B[5]);
  nand nand_7 (nand_1_out[6], A[6], B[6]);
  nand nand_8 (nand_1_out[7], A[7], B[7]);
  and and_1 (and_1_out, CarryFlag, CarryEn);
  nor nor_6 (nor_6_out, CarryEn, not_6_out);
  nor nor_7 (nor_2_out[4], not_7_out, Passthrough);
  nor nor_8 (nor_2_out[5], not_8_out, Passthrough);
  nor nor_9 (nor_2_out[6], not_9_out, Passthrough);
  nor nor_10 (nor_2_out[7], not_10_out, Passthrough);
  nor nor_11 (nor_11_out, and_1_out, nor_6_out);
  nor nor_12 (nor_12_out, nor_11_out, Passthrough);
  Adder adder_1 (.a(A), .b(nor_2_out), .out({Negative, adder_1_out}), .cin(nor_12_out), .cout(CarryOut));
  nor nor_13 (nor_13_out, A[7], B[7]);
  Multiplexer #(.width(8)) multiplexer_1 (
    .in0({Negative, adder_1_out}), .in1(nand_1_out), .out(Result), .sel(nor_1_out));
  nor nor_14 (nor_14_out, Result[0], Result[1]);
  nor nor_15 (nor_15_out, Result[4], Result[5]);
  and and_2 (Overflow, Negative, nor_13_out);
  nor nor_16 (nor_16_out, Result[2], Result[3]);
  nor nor_17 (nor_17_out, Result[6], Result[7]);
  and and_3 (Zero, nor_14_out, nor_15_out, nor_16_out, nor_17_out);
endmodule

module TOverwrite (
  input  D,
  input  Overwrite,
  input  TEnable,
  input  CLK,
  output Q
);

  wire and_1_out, and_2_out, nand_1_out, nand_2_out, nand_3_out, nand_4_out, nand_5_out, nand_6_out,
       nor_1_out, nor_3_out, not_1_out, not_2_out, not_3_out, not_4_out, not_5_out;

  not not_1 (not_1_out, CLK);
  not not_2 (not_2_out, not_1_out);
  not not_3 (not_3_out, not_2_out);
  not not_4 (not_4_out, Overwrite);
  and and_1 (and_1_out, TEnable, nor_1_out);
  nor nor_1 (nor_1_out, CLK, not_3_out);
  and and_2 (and_2_out, and_1_out, not_4_out);
  nand nand_1 (nand_1_out, Q, and_2_out);
  nand nand_2 (nand_2_out, and_2_out, nor_3_out);
  not not_5 (not_5_out, D);
  nand nand_3 (nand_3_out, not_5_out, Overwrite);
  nand nand_4 (nand_4_out, D, Overwrite);
  nand nand_5 (nand_5_out, nand_1_out, nand_3_out);
  nand nand_6 (nand_6_out, nand_4_out, nand_2_out);
  nor nor_2 (Q, nand_5_out, nor_3_out);
  nor nor_3 (nor_3_out, Q, nand_6_out);
endmodule

module PC (
  input  [15:0] Addr,
  input  OverwriteHIGH,
  input  OverwriteLOW,
  input  CLK,
  output [15:0] Q
);

  TOverwrite toverwrite_1 (.D(Addr[0]), .Overwrite(OverwriteLOW), .TEnable(1'b1), .CLK(CLK), .Q(Q[0]));
  TOverwrite toverwrite_2 (.D(Addr[8]), .Overwrite(OverwriteHIGH), .TEnable(1'b1), .CLK(Q[7]), .Q(Q[8]));
  TOverwrite toverwrite_3 (.D(Addr[1]), .Overwrite(OverwriteLOW), .TEnable(1'b1), .CLK(Q[0]), .Q(Q[1]));
  TOverwrite toverwrite_4 (.D(Addr[9]), .Overwrite(OverwriteHIGH), .TEnable(1'b1), .CLK(Q[8]), .Q(Q[9]));
  TOverwrite toverwrite_5 (.D(Addr[2]), .Overwrite(OverwriteLOW), .TEnable(1'b1), .CLK(Q[1]), .Q(Q[2]));
  TOverwrite toverwrite_6 (.D(Addr[10]), .Overwrite(OverwriteHIGH), .TEnable(1'b1), .CLK(Q[9]), .Q(Q[10]));
  TOverwrite toverwrite_7 (.D(Addr[3]), .Overwrite(OverwriteLOW), .TEnable(1'b1), .CLK(Q[2]), .Q(Q[3]));
  TOverwrite toverwrite_8 (.D(Addr[11]), .Overwrite(OverwriteHIGH), .TEnable(1'b1), .CLK(Q[10]), .Q(Q[11]));
  TOverwrite toverwrite_9 (.D(Addr[4]), .Overwrite(OverwriteLOW), .TEnable(1'b1), .CLK(Q[3]), .Q(Q[4]));
  TOverwrite toverwrite_10 (.D(Addr[12]), .Overwrite(OverwriteHIGH), .TEnable(1'b1), .CLK(Q[11]), .Q(Q[12]));
  TOverwrite toverwrite_11 (.D(Addr[5]), .Overwrite(OverwriteLOW), .TEnable(1'b1), .CLK(Q[4]), .Q(Q[5]));
  TOverwrite toverwrite_12 (.D(Addr[13]), .Overwrite(OverwriteHIGH), .TEnable(1'b1), .CLK(Q[12]), .Q(Q[13]));
  TOverwrite toverwrite_13 (.D(Addr[6]), .Overwrite(OverwriteLOW), .TEnable(1'b1), .CLK(Q[5]), .Q(Q[6]));
  TOverwrite toverwrite_14 (.D(Addr[14]), .Overwrite(OverwriteHIGH), .TEnable(1'b1), .CLK(Q[13]), .Q(Q[14]));
  TOverwrite toverwrite_15 (.D(Addr[7]), .Overwrite(OverwriteLOW), .TEnable(1'b1), .CLK(Q[6]), .Q(Q[7]));
  TOverwrite toverwrite_16 (.D(Addr[15]), .Overwrite(OverwriteHIGH), .TEnable(1'b1), .CLK(Q[14]), .Q(Q[15]));
endmodule

module InstrLenDec (
  input  [7:0] Instr,
  output Len3,
  output Len2,
  output Len1
);

  wire nand_1_out, nand_2_out, nand_3_out, nand_4_out, nor_1_out, nor_2_out, not_1_out, not_2_out, not_3_out,
       not_4_out;

  not not_1 (not_1_out, Len1);
  and and_1 (Len3, Instr[7], not_1_out, Instr[6]);
  nor nor_1 (nor_1_out, Instr[4], Instr[6], Instr[7]);
  not not_2 (not_2_out, Instr[5]);
  not not_3 (not_3_out, Instr[4]);
  not not_4 (not_4_out, Instr[5]);
  nand nand_1 (nand_1_out, nor_1_out, not_2_out);
  nand nand_2 (nand_2_out, nor_1_out, Instr[5]);
  nand nand_3 (nand_3_out, Instr[4], Instr[5], Instr[6], Instr[7]);
  nor nor_2 (nor_2_out, not_3_out, not_4_out, Instr[6], Instr[7]);
  nand nand_4 (nand_4_out, nand_1_out, nand_2_out, nand_3_out);
  or or_1 (Len1, nand_4_out, nor_2_out);
  nor nor_3 (Len2, Len3, Len1);
endmodule

module InstrDecoder (
  input  [7:0] Instr,
  output Stop,
  output Add,
  output Sub,
  output CarryEn,
  output BitNAND,
  output Cmp,
  output ImmIR1,
  output ImmIR2,
  output Jmp,
  output JmpZero,
  output JmpNeg,
  output JmpCarry,
  output JmpOver,
  output Push,
  output Pop,
  output Ret,
  output [1:0] Call,
  output StoreRel,
  output LoadRel,
  output Store,
  output Load,
  output ProgramLoad
);

  wire nand_1_out, nor_1_out, nor_2_out, nor_4_out, nor_5_out, nor_8_out, nor_9_out, nor_10_out, nor_12_out,
       nor_13_out, nor_17_out, nor_18_out, nor_19_out, not_1_out, not_2_out, not_3_out, not_4_out, not_5_out,
       not_6_out, not_7_out, not_8_out, not_9_out, not_10_out;

  not not_1 (not_1_out, Instr[0]);
  not not_2 (not_2_out, Instr[1]);
  and and_1 (Stop, not_1_out, not_2_out, nor_1_out);
  and and_2 (Ret, Instr[0], nor_1_out);
  not not_3 (not_3_out, Instr[4]);
  not not_4 (not_4_out, Instr[5]);
  not not_5 (not_5_out, Instr[6]);
  not not_6 (not_6_out, Instr[7]);
  nor nor_1 (nor_1_out, Instr[7], Instr[6], Instr[5], Instr[4]);
  and and_3 (Call[1], nor_1_out, not_1_out, Instr[1]);
  nor nor_2 (nor_2_out, Instr[7], Instr[6], Instr[5], not_3_out);
  not not_7 (not_7_out, Instr[0]);
  not not_8 (not_8_out, Instr[1]);
  not not_9 (not_9_out, Instr[3]);
  not not_10 (not_10_out, nor_19_out);
  nor nor_3 (Pop, Instr[7], Instr[6], not_4_out, Instr[4]);
  nand nand_1 (nand_1_out, not_7_out, nor_2_out);
  and and_4 (Store, Instr[0], nor_2_out);
  and and_5 (Cmp, nor_2_out, Instr[1]);
  nor nor_4 (nor_4_out, not_8_out, not_9_out);
  nor nor_5 (nor_5_out, Call[0], not_10_out);
  nor nor_6 (ProgramLoad, Instr[7], Instr[6], not_4_out, not_3_out);
  nor nor_7 (Push, nand_1_out, Cmp);
  and and_6 (Call[0], nor_19_out, nor_4_out);
  nor nor_8 (nor_8_out, Instr[7], not_5_out, Instr[5], Instr[4]);
  and and_7 (JmpCarry, Instr[2], nor_5_out);
  and and_8 (JmpNeg, nor_5_out, Instr[1]);
  nor nor_9 (nor_9_out, Instr[7], not_5_out, Instr[5], not_3_out);
  nor nor_10 (nor_10_out, Instr[7], not_5_out, not_4_out, not_3_out);
  nor nor_11 (StoreRel, Instr[7], not_5_out, not_4_out, Instr[4]);
  and and_9 (JmpZero, nor_5_out, Instr[0]);
  and and_10 (JmpOver, nor_5_out, Instr[3]);
  or or_1 (Add, nor_8_out, nor_9_out, nor_17_out);
  nor nor_12 (nor_12_out, not_6_out, Instr[6], Instr[5], Instr[4]);
  nor nor_13 (nor_13_out, JmpCarry, JmpZero, JmpNeg, JmpOver);
  nor nor_14 (LoadRel, not_6_out, Instr[6], Instr[5], not_3_out);
  or or_2 (CarryEn, nor_12_out, nor_9_out);
  and and_11 (Jmp, nor_5_out, nor_13_out);
  nor nor_15 (ImmIR1, not_6_out, Instr[6], not_4_out, Instr[4]);
  or or_3 (Sub, nor_10_out, nor_12_out, nor_18_out);
  nor nor_16 (BitNAND, not_6_out, Instr[6], not_4_out, not_3_out);
  nor nor_17 (nor_17_out, not_6_out, not_5_out, Instr[5], Instr[4]);
  nor nor_18 (nor_18_out, not_6_out, not_5_out, Instr[5], not_3_out);
  or or_4 (ImmIR2, nor_18_out, nor_17_out);
  nor nor_19 (nor_19_out, not_6_out, not_5_out, not_4_out, Instr[4]);
  nor nor_20 (Load, not_6_out, not_5_out, not_4_out, not_3_out);
endmodule

module InstrFetchRing (
  input  InstrLen3,
  input  InstrLen2,
  input  InstrLen1,
  input  RST,
  input  CLK,
  output WriteIR0,
  output WriteIR1,
  output WriteIR2,
  output Finished
);

  wire and_1_out, and_2_out, and_3_out, nor_1_out, not_1_out, or_1_out, or_2_out, toverwrite_4_q;

  not not_1 (not_1_out, CLK);
  nor nor_1 (nor_1_out, not_1_out, Finished);
  TOverwrite toverwrite_1 (.D(1'b1), .Overwrite(RST), .TEnable(WriteIR0), .CLK(nor_1_out), .Q(WriteIR0));
  and and_1 (and_1_out, InstrLen1, WriteIR1);
  or or_1 (or_1_out, WriteIR1, WriteIR0);
  TOverwrite toverwrite_2 (.Overwrite(RST), .TEnable(or_1_out), .CLK(nor_1_out), .Q(WriteIR1));  // open: D
  and and_2 (and_2_out, InstrLen2, WriteIR2);
  or or_2 (or_2_out, WriteIR2, WriteIR1);
  TOverwrite toverwrite_3 (.Overwrite(RST), .TEnable(or_2_out), .CLK(nor_1_out), .Q(WriteIR2));  // open: D
  and and_3 (and_3_out, InstrLen3, toverwrite_4_q);
  or or_3 (Finished, and_1_out, and_2_out, and_3_out);
  TOverwrite toverwrite_4 (.Overwrite(RST), .TEnable(WriteIR2), .CLK(nor_1_out), .Q(toverwrite_4_q));  // open: D
endmodule

module InstrStageRing (
  input  [1:0] Call,
  input  Ret,
  input  Pop,
  input  Push,
  input  RST,
  input  CLK,
  output GenericStage,
  output [1:0] StackStorePC,
  output SetSPtoBPDec,
  output [1:0] StackLoadPC,
  output SetBPtoSP,
  output [1:0] SetPC,
  output IncSP,
  output DecSP,
  output StackStoreBP,
  output StackLoadBP,
  output StackStoreReg,
  output StackLoadReg,
  output Finished
);

  wire and_1_out, and_6_out, and_7_out, and_14_out, and_15_out, nand_1_out, nand_2_out, nand_3_out,
       nand_4_out, nand_6_out, nand_8_out, nand_9_out, nand_10_out, nor_1_out, nor_2_out, not_1_out,
       not_2_out, not_3_out, not_4_out, or_1_out, or_2_out, or_3_out, or_4_out, or_5_out, or_6_out, or_7_out,
       or_8_out, SevenStage_out, toverwrite_1_q, toverwrite_2_q, toverwrite_3_q, toverwrite_4_q,
       toverwrite_5_q, toverwrite_6_q, toverwrite_7_q, toverwrite_9_q, TwoStage_out;

  not not_1 (not_1_out, RST);
  or SevenStage (SevenStage_out, Call[0], Call[1]);
  or TwoStage (TwoStage_out, Pop, Push);
  nor nor_1 (nor_1_out, Call[0], Ret, Pop, Push);
  not not_2 (not_2_out, not_1_out);
  not not_3 (not_3_out, not_2_out);
  not not_4 (not_4_out, CLK);
  and and_1 (and_1_out, RST, not_3_out);
  nor nor_2 (nor_2_out, not_4_out, Finished);
  TOverwrite toverwrite_1 (
    .D(1'b1), .Overwrite(and_1_out), .TEnable(toverwrite_1_q), .CLK(nor_2_out), .Q(toverwrite_1_q));
  or or_1 (or_1_out, toverwrite_2_q, toverwrite_1_q);
  TOverwrite toverwrite_2 (.Overwrite(and_1_out), .TEnable(or_1_out), .CLK(nor_2_out), .Q(toverwrite_2_q));  // open: D
  and and_2 (GenericStage, nor_1_out, toverwrite_2_q);
  and and_3 (StackStoreReg, toverwrite_2_q, Push);
  nand nand_1 (nand_1_out, toverwrite_2_q, Pop);
  and and_4 (SetSPtoBPDec, toverwrite_2_q, Ret);
  and and_5 (StackStoreBP, toverwrite_2_q, SevenStage_out);
  and and_6 (and_6_out, nor_1_out, toverwrite_3_q);
  or or_2 (or_2_out, toverwrite_3_q, toverwrite_2_q);
  TOverwrite toverwrite_3 (.Overwrite(and_1_out), .TEnable(or_2_out), .CLK(nor_2_out), .Q(toverwrite_3_q));  // open: D
  and and_7 (and_7_out, TwoStage_out, toverwrite_4_q);
  or or_3 (or_3_out, toverwrite_4_q, toverwrite_3_q);
  nand nand_2 (nand_2_out, toverwrite_3_q, Push);
  and and_8 (StackLoadReg, toverwrite_3_q, Pop);
  and and_9 (StackLoadPC[1], toverwrite_3_q, Ret);
  nand nand_3 (nand_3_out, toverwrite_3_q, SevenStage_out);
  TOverwrite toverwrite_4 (.Overwrite(and_1_out), .TEnable(or_3_out), .CLK(nor_2_out), .Q(toverwrite_4_q));  // open: D
  nand nand_4 (nand_4_out, toverwrite_4_q, Ret);
  and and_10 (StackStorePC[0], toverwrite_4_q, SevenStage_out);
  or or_4 (or_4_out, toverwrite_5_q, toverwrite_4_q);
  TOverwrite toverwrite_5 (.Overwrite(and_1_out), .TEnable(or_4_out), .CLK(nor_2_out), .Q(toverwrite_5_q));  // open: D
  nand nand_5 (DecSP, nand_8_out, nand_4_out, nand_1_out);
  and and_11 (StackLoadPC[0], toverwrite_5_q, Ret);
  nand nand_6 (nand_6_out, toverwrite_5_q, SevenStage_out);
  or or_5 (or_5_out, toverwrite_6_q, toverwrite_5_q);
  nand nand_7 (IncSP, nand_9_out, nand_6_out, nand_10_out, nand_2_out, nand_3_out);
  TOverwrite toverwrite_6 (.Overwrite(and_1_out), .TEnable(or_5_out), .CLK(nor_2_out), .Q(toverwrite_6_q));  // open: D
  and and_12 (StackStorePC[1], toverwrite_6_q, SevenStage_out);
  or or_6 (or_6_out, toverwrite_7_q, toverwrite_6_q);
  nand nand_8 (nand_8_out, toverwrite_6_q, Ret);
  TOverwrite toverwrite_7 (.Overwrite(and_1_out), .TEnable(or_6_out), .CLK(nor_2_out), .Q(toverwrite_7_q));  // open: D
  and and_13 (StackLoadBP, toverwrite_7_q, Ret);
  nand nand_9 (nand_9_out, toverwrite_7_q, Call[0]);
  nand nand_10 (nand_10_out, toverwrite_7_q, Call[1]);
  and and_14 (and_14_out, Ret, SetBPtoSP);
  or or_7 (or_7_out, SetBPtoSP, toverwrite_7_q);
  TOverwrite toverwrite_8 (.Overwrite(and_1_out), .TEnable(or_7_out), .CLK(nor_2_out), .Q(SetBPtoSP));  // open: D
  not not_5 (SetPC[0], nand_9_out);
  not not_6 (SetPC[1], nand_10_out);
  and and_15 (and_15_out, SevenStage_out, toverwrite_9_q);
  or or_8 (or_8_out, toverwrite_9_q, SetBPtoSP);
  or or_9 (Finished, and_6_out, and_14_out, and_7_out, and_15_out);
  TOverwrite toverwrite_9 (.Overwrite(and_1_out), .TEnable(or_8_out), .CLK(nor_2_out), .Q(toverwrite_9_q));  // open: D
endmodule
